// Logisim project CU.circ as structural Verilog: 1 circuit, main circuit main
module main (
  input  MOV,
  input  MOI,
  input  LOAD,
  input  STORE,
  input  ADD,
  input  ADI,
  input  SUB,
  input  SUI,
  input  AND,
  input  ANI,
  input  OR,
  input  ORI,
  input  HLT,
  input  CLK,
  output STAGE_1,
  output STAGE_2,
  output STAGE_3,
  output STAGE_4,
  output STAGE_5
);

  D_Flip_Flop d_ff_1 (.clk(CLK), .D(STAGE_5), .Q(STAGE_1));  // open: Qn, preset, en, reset
  D_Flip_Flop d_ff_2 (.clk(CLK), .D(STAGE_1), .Q(STAGE_2));  // open: Qn, preset, en, reset
  D_Flip_Flop d_ff_3 (.clk(CLK), .D(STAGE_2), .Q(STAGE_3));  // open: Qn, preset, en, reset
  D_Flip_Flop d_ff_4 (.clk(CLK), .D(STAGE_3), .Q(STAGE_4));  // open: Qn, preset, en, reset
  D_Flip_Flop d_ff_5 (.clk(CLK), .D(STAGE_4), .Q(STAGE_5));  // open: Qn, preset, en, reset
endmodule
